# Fritzing sketch Actual Multiplexer (saved by Fritzing 0.9.3b)
breadboards: 2

parts:
  Mod1 = Raspberry Pi Pico
  Mod2 = KY-023 Dual Axis Joystick Module [package="Breakout board"]
  Mod3 = KY-023 Dual Axis Joystick Module [package="Breakout board"]
  R1 = Trimmer Potentiometer [maximum_resistance=10kΩ package=THT]
  R2 = Trimmer Potentiometer [maximum_resistance=10kΩ package=THT]

nets:
  GND: Mod1.pin_3, Mod1.pin_8, Mod1.pin_13, Mod1.pin_18, Mod1.pin_23, Mod1.pin_28, Mod1.pin_33, Mod1.pin_38, Mod2.GND, Mod3.GND, R1.leg2, R2.leg2
  N1: Mod1.pin_26, Mod2.+5V, R2.leg1
  N2: Mod1.pin_27, Mod3.+5V, R1.leg1
  N3: Mod1.pin_29, Mod2.SW, Mod3.SW
  N4: Mod1.pin_31, Mod2.VRy, Mod3.VRy
  N5: Mod1.pin_32, Mod2.VRx, Mod3.VRx
  N6: Mod1.pin_34, R1.wiper, R2.wiper

custom parts:
  Raspberry Pi Pico: Raspberry Pi Pico. Based around the RP2040 microcontroller the Pico is a low cost microcontroller device bringing Raspberry Pi quality, cost, and easy of use to the microcontroller space. Jan 2021, Split part in to two versions: tht (this one) and SMD. This one will drill holes for a .1 in header in pcb to allow plugging in the module as well as providing pads to solder the module to the top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
  KY-023 Dual Axis Joystick Module: KY-023 Dual-Axis Joystick Module.
