# Fritzing sketch Multiplexer (saved by Fritzing 0.9.3b)
breadboards: 1

parts:
  R1 = Resistor [tolerance=±5% resistance=10k package=THT]
  Q1 = NPN-Transistor [package="TO92 [THT]"]
  R2 = Resistor [tolerance=±5% resistance=1k package=THT]
  Mod1 = Raspberry Pi Pico
  Q2 = NPN-Transistor [package="TO92 [THT]"]
  Q3 = NPN-Transistor [package="TO92 [THT]"]
  R4 = Trimmer Potentiometer [maximum_resistance=10kΩ package=THT]
  R3 = Trimmer Potentiometer [maximum_resistance=10kΩ package=THT]

nets:
  N1: R1.Pin_0, Mod1.pin_29, Q3.B
  N2: R1.Pin_1, Q1.B
  N3: Q1.E, R2.Pin_1
  N4: Q1.C, Mod1.pin_3, Mod1.pin_8, Mod1.pin_13, Mod1.pin_18, Mod1.pin_23, Mod1.pin_28, Mod1.pin_33, Mod1.pin_38, Mod1.pin_42, R4.leg2, R3.leg2
  N5: R2.Pin_0, Mod1.pin_37, Q2.B, R4.leg1, R3.leg1
  N6: Mod1.pin_31, Q2.E, Q3.E
  N7: Q2.C, R4.wiper
  N8: Q3.C, R3.wiper

custom parts:
  Raspberry Pi Pico: Raspberry Pi Pico. Based around the RP2040 microcontroller the Pico is a low cost microcontroller device bringing Raspberry Pi quality, cost, and easy of use to the microcontroller space. Jan 2021, Split part in to two versions: tht (this one) and SMD. This one will drill holes for a .1 in header in pcb to allow plugging in the module as well as providing pads to solder the module to the top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
